// Logisim project Logisim.circ as structural Verilog: 1 circuit, main circuit main
module main (
  input  A,
  input  B,
  input  C,
  input  D,
  input  E,
  input  F,
  output out_7,
  output out_8,
  output out_9,
  output out_10
);

  wire and_2_out, and_3_out, and_4_out, and_5_out, and_6_out, and_7_out, and_8_out, and_9_out, and_10_out,
       and_11_out, and_12_out, C_out, I_C_out, I_D_out, I_E_out, S_C_out, S_D_out;

  and and_1 (out_7, ~A, ~B, ~C);  // AND_Gate
  and and_2 (and_2_out, ~A, B, ~C);  // AND_Gate
  and and_3 (and_3_out, ~A, B, ~D);  // AND_Gate
  and and_4 (and_4_out, ~A, B, ~E, ~F);  // AND_Gate
  and and_5 (and_5_out, A, C, D, F);
  and and_6 (and_6_out, A, C, D, E);
  and and_7 (and_7_out, A, ~C);  // AND_Gate
  and and_8 (and_8_out, A, ~D);  // AND_Gate
  and and_9 (and_9_out, ~A, ~B, C);  // AND_Gate
  and and_10 (and_10_out, A, ~E, ~F);  // AND_Gate
  and and_11 (and_11_out, ~A, C, D, F);  // AND_Gate
  and and_12 (and_12_out, ~A, C, D, E);  // AND_Gate
  or or_1 (out_10, and_7_out, and_8_out, and_9_out, and_10_out, and_11_out, and_12_out);
  or or_2 (out_8, and_2_out, and_3_out, and_4_out);
  or or_3 (out_9, and_5_out, and_6_out);
  or S_D (S_D_out, out_7, out_8, out_9);
  or S_C (S_C_out, out_8, out_9, out_10);
  or u_C (C_out, out_8, out_9, out_10);
  or I_E (I_E_out, out_8, out_10);
  or I_C (I_C_out, out_8, out_9, out_10);
  or I_D (I_D_out, out_7, out_9);
  _7_Segment_Display u_7_segment_display_1 (
    .g(C_out), .f(out_10), .a(S_C_out), .b(S_D_out), .e(I_E_out), .d(I_C_out), .c(I_D_out));  // open: dp

  // Notes on the sheet:
  //   Categoria: 1 
  //   ~A~B~C
  //   Categoria 2:
  //   Categoria 3:
  //   ACDF + ACDE
  //   Erro:
  //   ~AB~C + ~AB~D +~AB~E~F
  //   A~C + A~D + ~A~BC + A~E~F + ~ACDF + ~ACDE
  //   Legenda:
  //   S: Superior
  //   I: Inferior
  //   D: Direita
  //   E:Esquerdo
  //   C: Centro
  //   S E
endmodule
